# Fritzing sketch raindrum (saved by Fritzing 0.9.9b)
breadboards: 1

parts:
  Part1 = Arduino Mega ADK (Rev3)
  U1 = MIDI_CONN_FEMALE [package=din_5_female]
  R1 = Resistor [tolerance=±5% resistance=220 package="0402 [SMD]"]
  R2 = Resistor [tolerance=±5% resistance=220 package="0402 [SMD]"]
  RGB_SMD_LED1 = SMD RGB LED (WS2812) [package=5050]
  RGB_SMD_LED2 = SMD RGB LED (WS2812) [package=5050]
  RGB_SMD_LED3 = SMD RGB LED (WS2812) [package=5050]
  RGB_SMD_LED4 = SMD RGB LED (WS2812) [package=5050]
  RGB_SMD_LED5 = SMD RGB LED (WS2812) [package=5050]
  RGB_SMD_LED6 = SMD RGB LED (WS2812) [package=5050]
  YL-83_-_Detection_Board1 = YL-83 Rain Sensor - Detection Board
  YL-83_-_Control_Board1 = YL-83 Rain Sensor - Control Board
  YL-83_-_Detection_Board2 = YL-83 Rain Sensor - Detection Board
  YL-83_-_Control_Board2 = YL-83 Rain Sensor - Control Board
  YL-83_-_Detection_Board3 = YL-83 Rain Sensor - Detection Board
  YL-83_-_Control_Board3 = YL-83 Rain Sensor - Control Board
  YL-83_-_Detection_Board4 = YL-83 Rain Sensor - Detection Board
  YL-83_-_Control_Board4 = YL-83 Rain Sensor - Control Board
  YL-83_-_Detection_Board5 = YL-83 Rain Sensor - Detection Board
  YL-83_-_Control_Board5 = YL-83 Rain Sensor - Control Board
  YL-83_-_Detection_Board6 = YL-83 Rain Sensor - Detection Board
  YL-83_-_Control_Board6 = YL-83 Rain Sensor - Control Board

nets:
  N1: Part1.A0, YL-83_-_Control_Board1.AO
  N2: Part1.A1, YL-83_-_Control_Board2.AO
  N3: Part1.A2, YL-83_-_Control_Board3.AO
  N4: Part1.A3, YL-83_-_Control_Board4.AO
  N5: Part1.A4, YL-83_-_Control_Board5.AO
  N6: Part1.A5, YL-83_-_Control_Board6.AO
  VCC: Part1.3V3, RGB_SMD_LED1.VCC, RGB_SMD_LED2.VCC, RGB_SMD_LED3.VCC, RGB_SMD_LED4.VCC, RGB_SMD_LED5.VCC, RGB_SMD_LED6.VCC
  VCC_2: Part1.5V, R1.Pin_0, YL-83_-_Control_Board1.VCC, YL-83_-_Control_Board2.VCC, YL-83_-_Control_Board3.VCC, YL-83_-_Control_Board4.VCC, YL-83_-_Control_Board5.VCC, YL-83_-_Control_Board6.VCC
  GND: Part1.GND, U1.NC1, RGB_SMD_LED1.VSS, RGB_SMD_LED2.VSS, RGB_SMD_LED3.VSS, RGB_SMD_LED4.VSS, RGB_SMD_LED5.VSS, RGB_SMD_LED6.VSS, YL-83_-_Control_Board1.GND, YL-83_-_Control_Board2.GND, YL-83_-_Control_Board3.GND, YL-83_-_Control_Board4.GND, YL-83_-_Control_Board5.GND, YL-83_-_Control_Board6.GND
  N7: Part1.D1/TX0, R2.Pin_0
  N8: Part1.D7_PWM, RGB_SMD_LED5.DIn
  N9: U1.MIDI_IN, R1.Pin_1
  N10: U1.MIDI_OUT, R2.Pin_1
  N11: RGB_SMD_LED1.DIn, RGB_SMD_LED2.DOut
  N12: RGB_SMD_LED2.DIn, RGB_SMD_LED3.DOut
  N13: RGB_SMD_LED3.DIn, RGB_SMD_LED4.DOut
  N14: RGB_SMD_LED4.DIn, RGB_SMD_LED6.DOut
  N15: RGB_SMD_LED5.DOut, RGB_SMD_LED6.DIn
  N16: YL-83_-_Detection_Board1.POS, YL-83_-_Control_Board1.POS
  N17: YL-83_-_Detection_Board1.NEG, YL-83_-_Control_Board1.NEG
  N18: YL-83_-_Detection_Board2.POS, YL-83_-_Control_Board2.POS
  N19: YL-83_-_Detection_Board2.NEG, YL-83_-_Control_Board2.NEG
  N20: YL-83_-_Detection_Board3.POS, YL-83_-_Control_Board3.POS
  N21: YL-83_-_Detection_Board3.NEG, YL-83_-_Control_Board3.NEG
  N22: YL-83_-_Detection_Board4.POS, YL-83_-_Control_Board4.POS
  N23: YL-83_-_Detection_Board4.NEG, YL-83_-_Control_Board4.NEG
  N24: YL-83_-_Detection_Board5.POS, YL-83_-_Control_Board5.POS
  N25: YL-83_-_Detection_Board5.NEG, YL-83_-_Control_Board5.NEG
  N26: YL-83_-_Detection_Board6.POS, YL-83_-_Control_Board6.POS
  N27: YL-83_-_Detection_Board6.NEG, YL-83_-_Control_Board6.NEG

notes:
  The actual part I used looks a little different, but it's most important that the 3.3V of the Arduino is connected to the 5V/VCC and GND to GND, and the digital out to the DIN of the led. Then each 5V can be connected to the next, same for GND and the DO should be connected to the DIN of the next led.

custom parts:
  YL-83 Rain Sensor - Detection Board: The YL-83 is a rain sensor that has more resistance when dry and less resistance when wet. The module runs at 5V.
  YL-83 Rain Sensor - Control Board: The YL-83 is a rain sensor that has more resistance when dry and less resistance when wet. The module runs at 5V.
